// Logisim project battleship.circ as structural Verilog: 3 circuits, main circuit main
module main (
  input  [3:0] in_1,
  input  [3:0] in_2,
  input  in_3,
  output out_4,
  output out_5,
  output out_6,
  output out_7,
  output out_8
);

  Encoder encoder_1 (.Navio(in_1), .out_5(out_6));  // open: in_2, in_3, in_4, out_6, out_7, out_8
endmodule

module decodificador (
  input  A,
  input  B,
  output out_3,
  output out_4,
  output out_5,
  output out_6
);

  and and_1 (out_3, A, B);
  and and_2 (out_4, ~B, A);  // AND_Gate
  and and_3 (out_5, B, ~A);  // AND_Gate
  and and_4 (out_6, ~B, ~A);  // AND_Gate
endmodule

module Encoder (
  input  [3:0] Navio,
  input  [3:0] in_2,
  input  [3:0] in_3,
  input  [3:0] in_4,
  output out_5,
  output out_6,
  output out_7,
  output out_8
);

  wire and_1_out, and_2_out, and_3_out, and_4_out, and_5_out, and_6_out;

  and and_1 (and_1_out, ~Navio[3], ~Navio[2], Navio[0]);  // AND_Gate
  and and_2 (and_2_out, ~Navio[3], Navio[2], ~Navio[0]);  // AND_Gate
  and and_3 (and_3_out, Navio[3], ~Navio[1], Navio[0]);  // AND_Gate
  and and_4 (and_4_out, Navio[3], Navio[1], ~Navio[0]);  // AND_Gate
  and and_5 (and_5_out, ~in_2[3], ~in_2[2], ~in_2[0]);  // AND_Gate
  and and_6 (and_6_out, ~in_2[3], in_2[2], in_2[0]);  // AND_Gate
  and and_7 (out_7, in_3[3], in_3[1], in_3[0]);
  and and_8 (out_8, in_4[3], in_4[2], ~in_4[1], ~in_4[0]);  // AND_Gate
  or or_1 (out_5, and_1_out, and_2_out, and_3_out, and_4_out);
  or or_2 (out_6, and_5_out, and_6_out);
endmodule
